# Fritzing sketch Assignment3-4 (saved by Fritzing 0.9.3b)
breadboards: 1

parts:
  Composant2 = Arduino Ethernet Shield (Rev3)
  R1 = Resistor [tolerance=±5% resistance=220 package="2512 [SMD]"]
  Composant3 = Bluetooth HC-05 Macho

nets:
  N1: Composant2.D8, Composant3.TXD
  N2: Composant2.PWM_D9, Composant3.RXD
  N3: Composant2.A0, R1.Pin_1
  5V: Composant2.5V, Composant3.VCC
  GND: Composant2.GND, R1.Pin_0, Composant3.GND

notes:
  To water cup
  Adafruit Shield on top of UNO card
