# Fritzing sketch alhabash-nour-assignment-2 (saved by Fritzing 0.9.3b)
breadboards: 1

parts:
  Composant1 = Arduino Uno (Rev3)
  LCD1 = LCD screen
  Composant2 = Thumb Joystick
  R1 = Resistor [tolerance=±5% resistance=220 package=THT]
  LED1 = smd LED [color="Red (633nm)" package="0603 [SMD]"]
  LED2 = smd LED [color="Yellow (595nm)" package="0603 [SMD]"]
  LED4 = smd LED [color="Blue (430nm)" package="0603 [SMD]"]
  R2 = Resistor [tolerance=±5% resistance=220 package=THT]
  R3 = Resistor [tolerance=±5% resistance=220 package=THT]
  R4 = Resistor [tolerance=±5% resistance=220 package=THT]
  LED3 = smd LED [color="Green (565nm)" package="0603 [SMD]"]
  R5 = Rotary Potentiometer (Small) [maximum_resistance=100kΩ package=THT]
  R6 = Resistor [tolerance=±5% resistance=220 package=THT]
  J1 = Piezo Speaker
  BAT1 = BC9VPC [package=bc9vpc]  # not connected

nets:
  N1: Composant1.A0, Composant2.VERT
  N2: Composant1.A1, Composant2.HORZ
  N3: Composant1.D8, LCD1.DB7
  N4: Composant1.D9_PWM, LCD1.DB6
  N5: Composant1.D10_PWM/SS, LCD1.DB5
  N6: Composant1.D11_PWM/MOSI, LCD1.DB4
  N7: Composant1.D12/MISO, LCD1.E
  N8: Composant1.D13/SCK, LCD1.RS
  N9: Composant1.D2, Composant2.SEL
  N10: Composant1.D3_PWM, J1.pin2
  N11: Composant1.D4, LED3.anode
  N12: Composant1.D5_PWM, LED4.anode
  N13: Composant1.D6_PWM, LED2.anode
  N14: Composant1.D7, LED1.anode
  5V: Composant1.5V, LCD1.VDD, Composant2.VCC, R2.Pin_1, R4.Pin_0, R5.leg2
  GND: Composant1.GND, LCD1.VSS, LCD1.R/W, LCD1.LED-, Composant2.GND, R1.Pin_1, R3.Pin_1, R5.leg1, R6.Pin_0, J1.pin1
  N15: LCD1.V0, R5.wiper
  N16: LCD1.LED+, R6.Pin_1
  N17: R1.Pin_0, LED2.cathode
  N18: LED1.cathode, R3.Pin_0
  N19: LED4.cathode, R2.Pin_0
  N20: R4.Pin_1, LED3.cathode

notes:
  Simon Game Project
  -Nour AL-HABASH
  Cable side is "down direction"
