# Fritzing sketch FinalProject (saved by Fritzing 0.9.3b)
breadboards: 1

parts:
  Composant1 = Arduino Uno (Rev3)
  Composant3 = Triple Axis Accelerometer Breakout - ADXL335
  VCC1 = Battery block 9V  # not connected
  RF1 = nRF8001 Bluetooth LE Breakout
  J2 = Piezo Speaker

nets:
  N1: Composant1.A0, Composant3.XOUT
  N2: Composant1.A1, Composant3.YOUT
  N3: Composant1.A2, Composant3.ZOUT
  N4: Composant1.D8, RF1.REQ
  N5: Composant1.D11_PWM/MOSI, RF1.MOSI
  N6: Composant1.D12/MISO, RF1.MISO
  N7: Composant1.D13/SCK, RF1.SCK
  N8: Composant1.D2, RF1.RDY
  N9: Composant1.D3_PWM, J2.pin2
  N10: Composant1.D7, RF1.RST
  3V3: Composant1.3V3, Composant3.VCC
  5V: Composant1.5V, RF1.VIN
  GND: Composant1.GND, Composant3.GND, RF1.GND, J2.pin1

notes:
  Mini USB to PC (Serial Connection)

custom parts:
  nRF8001 Bluetooth LE Breakout: nRF8001 Breakout Board
